# Fritzing sketch weemos_hookup (saved by Fritzing 0.8.5b)
breadboards: 1

parts:
  WeMos_D1_Mini1 = WeMos D1 Mini
  Q1 = NPN-Transistor [package="TO92 [THT]"]
  IR1 = TSOP312.., 314.. [package=THT]
  LED1 = LED - 5mm [color="Red (633nm)" package="5 mm [THT]"]
  22R = Resistor [package="2010 [SMD]"]
  LED2 = LED - 5mm [color="Red (633nm)" package="5 mm [THT]"]
  LED3 = LED - 5mm [color="Red (633nm)" package="5 mm [THT]"]
  LED4 = LED - 5mm [color="Red (633nm)" package="5 mm [THT]"]
  22R_2 = Resistor [package="2010 [SMD]"]

nets:
  N1: WeMos_D1_Mini1.3V3, IR1.Vs
  N2: WeMos_D1_Mini1.5V, Q1.C
  N3: WeMos_D1_Mini1.D3, Q1.B
  N4: WeMos_D1_Mini1.D4, IR1.Data
  N5: WeMos_D1_Mini1.G, IR1.GND, LED1.cathode, LED4.cathode
  N6: Q1.E, 22R.Pin_0, 22R_2.Pin_0
  N7: LED1.anode, LED3.cathode
  N8: 22R.Pin_1, LED2.anode
  N9: LED2.cathode, LED4.anode
  N10: LED3.anode, 22R_2.Pin_1

custom parts:
  WeMos D1 Mini: The D1 mini is a mini wifi board based on ESP-8266EX.
